# Fritzing sketch fritizing (saved by Fritzing 0.9.3b)

parts:
  WeMos_D1_Mini1 = WeMos D1 Mini
  LED1 = LEDs [package=led10mm]
  LED2 = LEDs [package=led10mm]
  LED3 = LEDs [package=led10mm]
  LED4 = LEDs [package=led10mm]
  S1 = Round Pushbutton
  S2 = Round Pushbutton

nets:
  N1: WeMos_D1_Mini1.D0, LED1.C
  N2: WeMos_D1_Mini1.D1, LED2.C
  N3: WeMos_D1_Mini1.D2, LED3.C
  N4: WeMos_D1_Mini1.D3, LED4.C
  N5: WeMos_D1_Mini1.D5, S1.leg1
  N6: WeMos_D1_Mini1.D6, S2.leg1
  N7: WeMos_D1_Mini1.G, LED2.A

notes:
  #define LED_A D0
  #define LED_B D1
  #define LED_C D2
  #define LED_U D4
  #define slider D7
  #define msSwitch D6
