# Fritzing sketch Untitled Sketch (saved by Fritzing 0.9.3b)

parts:
  Part1 = ESP12E Motor Shield
  M1 = DC Motor  # not connected
  M2 = DC Motor  # not connected
  VCC1 = Battery block 9V
  U1 = NodeMCU V1.0  # not connected
  S1 = H-Bridge with L298N
  M3 = DC Motor
  M4 = DC Motor

nets:
  N1: Part1.D1, Part1.D5, Part1.D6, Part1.D7, Part1.D8, Part1.3V3, S1.IN1, S1.IN2, S1.IN3, S1.IN4
  N2: VCC1.-, S1.GND
  N3: VCC1.+, S1.12V
  N4: S1.M1-01, M3.pin_2
  N5: S1.M1-02, M3.pin_1
  N6: S1.M2-01, M4.pin_1
  N7: S1.M2-02, M4.pin_2

custom parts:
  ESP12E Motor Shield: ESP8266 WiFi Motor Drive Expansion Board For NodeMCU ESP-12E
  NodeMCU V1.0: ESP8266 based NodeMCU
  H-Bridge with L298N: h-bridge
